# Fritzing sketch 7segmant (saved by Fritzing 0.9.3b)
breadboards: 1

parts:
  Parça1 = Arduino Uno (Rev3)
  U1 = 7-SEGMENT-DISPLAY-1_-RED [package=7-segment-1_pth]
  VCC1 = Battery block 9V
  R1 = Resistor [tolerance=±5% resistance=220 package=THT]
  R2 = Resistor [tolerance=±5% resistance=220 package=THT]
  R3 = Resistor [tolerance=±5% resistance=220 package=THT]
  R4 = Resistor [tolerance=±5% resistance=220 package=THT]
  R5 = Resistor [tolerance=±5% resistance=220 package=THT]
  R7 = Resistor [tolerance=±5% resistance=220 package=THT]
  R8 = Resistor [tolerance=±5% resistance=220 package=THT]
  R9 = Resistor [tolerance=±5% resistance=220 package=THT]

nets:
  N1: Parça1.D8, R9.Pin_1
  N2: Parça1.D9_PWM, R5.Pin_0
  N3: Parça1.GND, U1.G1, U1.G2, VCC1.-
  N4: Parça1.D2, R3.Pin_1
  N5: Parça1.D3_PWM, R4.Pin_1
  N6: Parça1.D4, R2.Pin_0
  N7: Parça1.D5_PWM, R1.Pin_0
  N8: Parça1.D6_PWM, R7.Pin_1
  N9: Parça1.D7, R8.Pin_0
  N10: Parça1.VIN, VCC1.+
  N11: U1.E, R5.Pin_1
  N12: U1.D, R9.Pin_0
  N13: U1.C, R8.Pin_1
  N14: U1.DP, R7.Pin_0
  N15: U1.B, R3.Pin_0
  N16: U1.A, R4.Pin_0
  N17: U1.F, R2.Pin_1
  N18: U1.G, R1.Pin_1
