# Fritzing sketch LCD 5110 (saved by Fritzing 0.9.2b)
breadboards: 1

parts:
  Nokia_5110_LCD_Module1 = Nokia 5110 LCD
  Eleman1 = Arduino Uno (Rev3)

nets:
  N1: Nokia_5110_LCD_Module1.VCC, Nokia_5110_LCD_Module1.VCC_(out), Eleman1.D11_PWM/MOSI
  N2: Nokia_5110_LCD_Module1.GND, Nokia_5110_LCD_Module1.GND_(out), Eleman1.D12/MISO
  N3: Nokia_5110_LCD_Module1.SCE, Nokia_5110_LCD_Module1.SCE_(out), Eleman1.D10_PWM/SS
  N4: Nokia_5110_LCD_Module1.RST, Nokia_5110_LCD_Module1.RST_(out), Eleman1.D9_PWM
  N5: Nokia_5110_LCD_Module1.D/C, Nokia_5110_LCD_Module1.D/C_(out), Eleman1.D8
  N6: Nokia_5110_LCD_Module1.DN(MOSI), Nokia_5110_LCD_Module1.DN(MODI)_(out), Eleman1.5V
  N7: Nokia_5110_LCD_Module1.SCLK, Nokia_5110_LCD_Module1.SCLK_(out), Eleman1.3V3
  N8: Nokia_5110_LCD_Module1.LED, Nokia_5110_LCD_Module1.LED_(out), Eleman1.GND

custom parts:
  Nokia 5110 LCD: Nokia 5110 Graphic 84*48 LCD module such as the Sparkfun LCD-10168 or the clones from Ebay. There is example code for the Arduino available from the Sparkfun site in https://learn.sparkfun.com/tutorials/graphic-lcd-hookup-guide This is a 3.3V device, if you are running it from a 5V micro you need a 5V tolorant level translator such as the 74ahc367 to protect the signal imputs. Rafa G. did a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
