# Fritzing sketch Uzaktan kumandalı vantilator projesi roleli versiyon (saved by Fritzing 0.9.2b)
breadboards: 1

parts:
  U3 = RELAY [package=relay-jzc]
  M1 = DC Motor
  Eleman1 = Arduino Nano (Rev3.0)
  VCC1 = Battery
  VCC2 = Battery
  LED1 = LED - 5mm [color="Red (633nm)" package="5 mm [THT]"]
  LED2 = LED - 5mm [color="Red (633nm)" package="5 mm [THT]"]
  LED3 = LED - 5mm [color="Red (633nm)" package="5 mm [THT]"]
  D1 = Rectifier Diode [part_number=1N4001 package="300 mil [THT]"]
  R1 = Resistor [tolerance=±5% resistance=220 package=THT]
  R2 = Resistor [tolerance=±5% resistance=220 package=THT]
  R3 = Resistor [tolerance=±5% resistance=220 package=THT]
  IR1 = TSOP312.., 314.. [package=THT]
  Q1 = NPN-Transistor [package="TO92 [THT]"]
  R4 = Resistor [tolerance=±5% resistance=220 package=THT]
  J1 = Piezo Speaker

nets:
  N1: U3.COIL2, U3.MAIN, Eleman1.5V, LED2.anode, D1.cathode, R3.Pin_0, IR1.Vs
  N2: U3.NC, M1.pin_1
  N3: U3.COIL1, Q1.C
  GND: M1.pin_2, Eleman1.GND, VCC2.-, LED1.anode, R1.Pin_0, R2.Pin_0, IR1.GND, Q1.E, J1.pin1
  N4: Eleman1.D3, IR1.Data
  N5: Eleman1.D4, J1.pin2
  N6: Eleman1.D8, R4.Pin_0
  N7: Eleman1.D9, LED3.anode
  N8: VCC1.-, VCC2.+
  N9: VCC1.+, D1.anode
  N10: LED1.cathode, R3.Pin_1
  N11: LED2.cathode, R2.Pin_1
  N12: LED3.cathode, R1.Pin_1
  N13: Q1.B, R4.Pin_1
