# Fritzing sketch elektronikorg (saved by Fritzing 0.9.3b)
breadboards: 2

parts:
  SPKR1 = Loudspeaker
  U1 = 555 Timer [package="DIP8 [THT]"]
  R1 = Resistor [tolerance=±5% resistance=4.2k package=THT]
  C1 = Electrolytic Capacitor [capacitance=100nF voltage=16V package="100 mil [THT, electrolytic]"]
  VCC1 = Battery block 9V
  R2 = Resistor [tolerance=±5% resistance=1k package=THT]
  R3 = Resistor [tolerance=±5% resistance=1k package=THT]
  R4 = Resistor [tolerance=±5% resistance=1k package=THT]
  R5 = Resistor [tolerance=±5% resistance=1k package=THT]
  R6 = Resistor [tolerance=±5% resistance=1k package=THT]
  R7 = Resistor [tolerance=±5% resistance=1k package=THT]
  R8 = Resistor [tolerance=±5% resistance=1k package=THT]
  S1 = Pushbutton [package="[SMD]"]
  S2 = Pushbutton [package="[SMD]"]
  S3 = Pushbutton [package="[SMD]"]
  S4 = Pushbutton [package="[SMD]"]
  S5 = Pushbutton [package="[SMD]"]
  S6 = Pushbutton [package="[SMD]"]
  S7 = Pushbutton [package="[SMD]"]
  C2 = Tantalum Capacitor [capacitance=1μF package="100 mil [THT, tantalum]"]
  C3 = Tantalum Capacitor [capacitance=1μF package="100 mil [THT, tantalum]"]

nets:
  N1: SPKR1.pin2, C1.-
  N2: U1.Ground, VCC1.-, C2.-, C3.-
  N3: U1.Trigger, U1.Threshold, R1.Pin_0, R2.Pin_1, S1.Pin_3, S1.Pin_4, S2.Pin_3, S2.Pin_4, S3.Pin_3, S3.Pin_4, S4.Pin_3, S4.Pin_4, S5.Pin_3, S5.Pin_4, S6.Pin_3, S6.Pin_4, S7.Pin_3, S7.Pin_4, C3.+
  N4: U1.Output, C1.+
  N5: U1.Reset, U1.Vcc_Supply_Voltage, R1.Pin_1, VCC1.+
  N6: U1.Control_Voltage, C2.+
  N7: R2.Pin_0, R8.Pin_1, S2.Pin_1, S2.Pin_2
  N8: R3.Pin_0, S7.Pin_1, S7.Pin_2
  N9: R3.Pin_1, R4.Pin_0, S6.Pin_1, S6.Pin_2
  N10: R4.Pin_1, R7.Pin_0, S5.Pin_1, S5.Pin_2
  N11: R5.Pin_0, R7.Pin_1, S1.Pin_1, S1.Pin_2
  N12: R5.Pin_1, R6.Pin_0, S4.Pin_1, S4.Pin_2
  N13: R6.Pin_1, R8.Pin_0, S3.Pin_1, S3.Pin_2
