# Fritzing sketch if else v2 (saved by Fritzing 0.9.2b)
breadboards: 1

parts:
  Eleman1 = Arduino Nano (Rev3.0)
  LED1 = LED - 5mm [color="Red (633nm)" package="5 mm [THT]"]
  LED2 = LED - 5mm [color="Red (633nm)" package="5 mm [THT]"]
  LED3 = LED - 5mm [color="Red (633nm)" package="5 mm [THT]"]
  LED4 = LED - 5mm [color="Red (633nm)" package="5 mm [THT]"]
  LED5 = LED - 5mm [color="Red (633nm)" package="5 mm [THT]"]
  LED6 = LED - 5mm [color="Red (633nm)" package="5 mm [THT]"]
  LED7 = LED - 5mm [color="Red (633nm)" package="5 mm [THT]"]
  LED8 = LED - 5mm [color="Red (633nm)" package="5 mm [THT]"]
  LED9 = LED - 5mm [color="Red (633nm)" package="5 mm [THT]"]
  LED10 = LED - 5mm [color="Red (633nm)" package="5 mm [THT]"]
  S1 = Pushbutton [package="[THT]"]
  R1 = Resistor [tolerance=±5% resistance=220 package=THT]
  R2 = Resistor [tolerance=±5% resistance=220 package=THT]
  R3 = Resistor [tolerance=±5% resistance=220 package=THT]
  R4 = Resistor [tolerance=±5% resistance=220 package=THT]
  R5 = Resistor [tolerance=±5% resistance=220 package=THT]
  R6 = Resistor [tolerance=±5% resistance=220 package=THT]
  R7 = Resistor [tolerance=±5% resistance=220 package=THT]
  R8 = Resistor [tolerance=±5% resistance=220 package=THT]
  R9 = Resistor [tolerance=±5% resistance=220 package=THT]
  R10 = Resistor [tolerance=±5% resistance=220 package=THT]
  R11 = Resistor [tolerance=±5% resistance=220 package=THT]

nets:
  N1: Eleman1.D2, S1.Pin_1, S1.Pin_2, R1.Pin_1
  N2: Eleman1.D3, LED1.anode
  N3: Eleman1.D4, LED2.anode
  N4: Eleman1.D5, LED3.anode
  N5: Eleman1.D6, LED4.anode
  N6: Eleman1.D7, LED5.anode
  N7: Eleman1.D8, LED6.anode
  N8: Eleman1.D9, LED7.anode
  N9: Eleman1.D10, LED8.anode
  N10: Eleman1.D11/MOSI, LED9.anode
  N11: Eleman1.D12/MISO, LED10.anode
  N12: LED1.cathode, R11.Pin_1
  N13: LED2.cathode, R10.Pin_1
  N14: LED3.cathode, R9.Pin_1
  N15: LED4.cathode, R8.Pin_1
  N16: LED5.cathode, R5.Pin_1
  N17: LED6.cathode, R4.Pin_1
  N18: LED7.cathode, R6.Pin_1
  N19: LED8.cathode, R7.Pin_1
  N20: LED9.cathode, R3.Pin_1
  N21: LED10.cathode, R2.Pin_1
  N22: S1.Pin_3, S1.Pin_4
  N23: R1.Pin_0, R2.Pin_0, R3.Pin_0, R4.Pin_0, R5.Pin_0, R6.Pin_0, R7.Pin_0, R8.Pin_0, R9.Pin_0, R10.Pin_0, R11.Pin_0
