# Fritzing sketch if else (saved by Fritzing 0.9.2b)
breadboards: 1

parts:
  Eleman1 = Arduino Uno (Rev3)
  LED1 = LED - 5mm [color="Red (633nm)" package="5 mm [THT]"]
  LED2 = LED - 5mm [color="Red (633nm)" package="5 mm [THT]"]
  LED3 = LED - 5mm [color="Red (633nm)" package="5 mm [THT]"]
  LED4 = LED - 5mm [color="Red (633nm)" package="5 mm [THT]"]
  R1 = Resistor [tolerance=±5% resistance=220 package=THT]
  R2 = Resistor [tolerance=±5% resistance=220 package=THT]
  R3 = Resistor [tolerance=±5% resistance=220 package=THT]
  R4 = Resistor [tolerance=±5% resistance=220 package=THT]
  S1 = Pushbutton [package="[THT]"]
  R5 = Resistor [tolerance=±5% resistance=220 package=THT]

nets:
  N1: Eleman1.D3_PWM, LED4.anode
  N2: Eleman1.D4, LED3.anode
  N3: Eleman1.D5_PWM, LED2.anode
  N4: Eleman1.D6_PWM, LED1.anode
  N5: Eleman1.D7, S1.Pin_1, S1.Pin_2, R5.Pin_1
  N6: Eleman1.5V, S1.Pin_3, S1.Pin_4
  N7: Eleman1.GND, R1.Pin_0, R2.Pin_0, R3.Pin_0, R4.Pin_0, R5.Pin_0
  N8: LED1.cathode, R3.Pin_1
  N9: LED2.cathode, R2.Pin_1
  N10: LED3.cathode, R1.Pin_1
  N11: LED4.cathode, R4.Pin_1
