# Fritzing sketch led animasyon (saved by Fritzing 0.9.2b)
breadboards: 1

parts:
  R1 = Resistor [tolerance=±5% resistance=220 package=THT]
  R2 = Resistor [tolerance=±5% resistance=220 package=THT]
  R3 = Resistor [tolerance=±5% resistance=220 package=THT]
  R4 = Resistor [tolerance=±5% resistance=220 package=THT]
  R5 = Resistor [tolerance=±5% resistance=220 package=THT]
  R6 = Resistor [tolerance=±5% resistance=220 package=THT]
  R7 = Resistor [tolerance=±5% resistance=220 package=THT]
  R8 = Resistor [tolerance=±5% resistance=220 package=THT]
  R9 = Resistor [tolerance=±5% resistance=220 package=THT]
  R10 = Resistor [tolerance=±5% resistance=220 package=THT]
  R11 = Resistor [tolerance=±5% resistance=220 package=THT]
  LED1 = LED - 5mm [color="Red (633nm)" package="5 mm [THT]"]
  LED2 = LED - 5mm [color="Red (633nm)" package="5 mm [THT]"]
  LED3 = LED - 5mm [color="Red (633nm)" package="5 mm [THT]"]
  LED4 = LED - 5mm [color="Red (633nm)" package="5 mm [THT]"]
  LED5 = LED - 5mm [color="Red (633nm)" package="5 mm [THT]"]
  LED6 = LED - 5mm [color="Red (633nm)" package="5 mm [THT]"]
  LED7 = LED - 5mm [color="Red (633nm)" package="5 mm [THT]"]
  LED8 = LED - 5mm [color="Red (633nm)" package="5 mm [THT]"]
  LED9 = LED - 5mm [color="Red (633nm)" package="5 mm [THT]"]
  LED10 = LED - 5mm [color="Red (633nm)" package="5 mm [THT]"]
  LED11 = LED - 5mm [color="Red (633nm)" package="5 mm [THT]"]
  Eleman1 = Arduino Nano (Rev3.0)

nets:
  N1: R1.Pin_0, R2.Pin_0, R3.Pin_0, R4.Pin_0, R5.Pin_0, R6.Pin_0, R7.Pin_0, R8.Pin_0, R9.Pin_0, R10.Pin_0, R11.Pin_0
  N2: R1.Pin_1, LED11.cathode
  N3: R2.Pin_1, LED7.cathode
  N4: R3.Pin_1, LED6.cathode
  N5: R4.Pin_1, LED10.cathode
  N6: R5.Pin_1, LED5.cathode
  N7: R6.Pin_1, LED4.cathode
  N8: R7.Pin_1, LED3.cathode
  N9: R8.Pin_1, LED2.cathode
  N10: R9.Pin_1, LED1.cathode
  N11: R10.Pin_1, LED9.cathode
  N12: R11.Pin_1, LED8.cathode
  N13: LED1.anode, Eleman1.D13/SCK
  N14: LED2.anode, Eleman1.D12/MISO
  N15: LED3.anode, Eleman1.D11/MOSI
  N16: LED4.anode, Eleman1.D10
  N17: LED5.anode, Eleman1.D9
  N18: LED6.anode, Eleman1.D8
  N19: LED7.anode, Eleman1.D7
  N20: LED8.anode, Eleman1.D6
  N21: LED9.anode, Eleman1.D5
  N22: LED10.anode, Eleman1.D4
  N23: LED11.anode, Eleman1.D3
