# Fritzing sketch polis çakarı (saved by Fritzing 0.9.2b)
breadboards: 1

parts:
  LED1 = LED - 3mm [color="Red (633nm)" package="3 mm [THT]"]
  LED2 = LED - 3mm [color="Red (633nm)" package="3 mm [THT]"]
  Eleman1 = Arduino Nano (Rev3.0)
  R1 = Resistor [tolerance=±5% resistance=220 package=THT]
  R2 = Resistor [tolerance=±5% resistance=220 package=THT]

nets:
  N1: LED1.cathode, R1.Pin_1
  N2: LED1.anode, Eleman1.D3
  N3: LED2.cathode, R2.Pin_1
  N4: LED2.anode, Eleman1.D4
  N5: Eleman1.GND, R1.Pin_0, R2.Pin_0

// code stored in the sketch: Untitled.ino

