# Fritzing sketch uzaktanfankod (saved by Fritzing 0.9.3b)
breadboards: 2

parts:
  Parça1 = Arduino Nano (Rev3.0)
  L298N1 = L298N DC motor driver
  M1 = DC Motor
  LED1 = LED - 3mm [color="Red (633nm)" package="3 mm [THT]"]
  LED2 = LED - 3mm [color="Red (633nm)" package="3 mm [THT]"]
  LED3 = LED - 3mm [color="Red (633nm)" package="3 mm [THT]"]
  R1 = Resistor [tolerance=±5% resistance=220 package="1206 [SMD]"]
  R2 = Resistor [tolerance=±5% resistance=220 package="1206 [SMD]"]
  R3 = Resistor [tolerance=±5% resistance=220 package="1206 [SMD]"]
  J1 = Piezo Speaker
  Mod1 = KY-022 Infrared Receiver Module [package="Breakout board"]
  LED4 = smd LED [color="Red (633nm)" package="0805 [SMD]"]
  LED5 = smd LED [color="Red (633nm)" package="0805 [SMD]"]
  LED6 = smd LED [color="Red (633nm)" package="0805 [SMD]"]
  LED7 = smd LED [color="Red (633nm)" package="0805 [SMD]"]
  R4 = Resistor [tolerance=±5% resistance=220 package=THT]
  R5 = Resistor [tolerance=±5% resistance=220 package=THT]
  R6 = Resistor [tolerance=±5% resistance=220 package=THT]
  R7 = Resistor [tolerance=±5% resistance=220 package=THT]
  D1 = Schottky Diode [part_number=1N5817 package="Melf DO-213 AB [SMD]"]

nets:
  GND: Parça1.GND, L298N1.GND, R2.Pin_0, R3.Pin_0, J1.pin1, Mod1.-, R4.Pin_0, R5.Pin_0, R6.Pin_0, R7.Pin_0, D1.cathode
  N1: Parça1.D3, Mod1.S
  N2: Parça1.D4, J1.pin2
  N3: Parça1.D8, LED6.anode
  N4: Parça1.D9, L298N1.ENB, L298N1.IN4
  N5: Parça1.D10, LED3.anode
  N6: Parça1.D11/MOSI, LED2.anode
  N7: Parça1.D12/MISO, LED1.anode
  N8: Parça1.D13/SCK, LED7.anode
  N9: L298N1.OUT3, M1.pin_2
  N10: L298N1.OUT4, M1.pin_1
  12V: L298N1.12V, R1.Pin_0, Mod1.Vin, LED5.anode
  N11: LED1.cathode, R7.Pin_1
  N12: LED2.cathode, R6.Pin_1
  N13: LED3.cathode, R3.Pin_1
  N14: R1.Pin_1, LED4.cathode
  N15: R2.Pin_1, LED6.cathode
  N16: LED4.anode, D1.anode
  N17: LED5.cathode, R4.Pin_1
  N18: LED7.cathode, R5.Pin_1

custom parts:
  L298N DC motor driver: 2x DC motor driver with 78M05 positive voltage regulator (7..35 V) L298N: max 46 V, 2 A Set 5 V Enable jumper to enable 5 V regultor (needed for the L298N) and +5 V output at screw terminal or supply external +5 V at screw terminal Set ENA and/or ENB to +5 V to enable motor permanently or supply ENA and/or ENB with PWM signal IN1 and IN2 set rotation directory for motor A (OUT1/OUT2) IN2 and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
  KY-022 Infrared Receiver Module: KY-022 IR receiver module, reacts to 38kHz infrared light.
